// Logisim project main.circ as structural Verilog: 1 circuit, main circuit main
module main (
  input  in_1
);

  wire and_2_out, and_4_out, and_5_out, and_6_out, and_7_out, and_8_out, and_9_out, clock_1_out,
       decoder_1_out0, decoder_1_out7, decoder_2_out0, decoder_2_out1, decoder_2_out3, decoder_2_out4,
       decoder_2_out5, decoder_2_out6, I_q, not_1_out, not_2_out, or_1_out, or_2_out, or_3_out;
  wire [0:0] AC_q;
  wire [1:0] decoder_2_out2;
  wire [1:1] and_3_out;
  wire [2:0] OPCODE_q, SC_q;
  wire [11:0] AR_q, multiplexer_1_out, PC_q;
  wire [15:0] AC_q_2, demultiplexer_1_out0, demultiplexer_1_out1, demultiplexer_1_out2, DR_q, IR_q,
       multiplexer_2_out, ram_1_data;

  Counter #(.width(12), .max('hfff)) PC (.Q(PC_q), .clk(decoder_2_out1), .clr(in_1));  // open: load, D, count, carry
  and and_1 (decoder_2_out2[1], decoder_2_out3, and_8_out);
  Multiplexer #(.select(2), .width(12), .enable("false")) multiplexer_1 (
    .in0(PC_q), .in1(IR_q[11:0]), .in2(demultiplexer_1_out1[11:0]), .out(multiplexer_1_out),
    .sel(decoder_2_out2));  // open: in3
  Register #(.width(12), .trigger("falling")) AR (.D(multiplexer_1_out), .Q(AR_q), .clk(and_2_out));  // open: en, clr
  and and_2 (and_2_out, or_1_out, clock_1_out);
  or or_1 (or_1_out, decoder_2_out2[0], decoder_2_out2[1], decoder_2_out0);
  and and_3 (and_3_out[1], decoder_2_out4, decoder_1_out0);
  Multiplexer #(.width(16), .enable("false")) multiplexer_2 (
    .in0(DR_q), .in1(AC_q_2), .out(multiplexer_2_out), .sel(and_9_out));
  and and_4 (and_4_out, decoder_2_out5, decoder_1_out0);
  Register #(.width(16)) IR (.D(demultiplexer_1_out0), .Q(IR_q), .clk(decoder_2_out1));  // open: en, clr
  or or_2 (or_2_out, and_4_out, and_9_out);
  Register #(.width(16), .trigger("high")) DR (
    .D(demultiplexer_1_out2), .Q(DR_q), .clk(and_3_out[1]));  // open: en, clr
  Register #(.width(16), .trigger("falling")) AC (
    .D(multiplexer_2_out), .Q({AC_q_2[14:0], AC_q[0]}), .clk(or_2_out));  // open: en, clr
  RAM #(.addrWidth(12), .dataWidth(16), .bus("separate")) ram_1 (
    .addr(AR_q), .din({AC_q_2[14:0], AC_q[0]}), .data(ram_1_data), .str(and_4_out), .clk(and_4_out));  // open: sel, ld, clr
  Register #(.width(1), .trigger("falling")) E (.D(1'b0), .Q(AC_q_2[15]), .clk(and_9_out));  // open: en, clr
  and and_5 (and_5_out, decoder_2_out4, and_7_out);
  Demultiplexer #(.select(2), .width(16), .enable("false")) demultiplexer_1 (
    .out0(demultiplexer_1_out0), .out1(demultiplexer_1_out1), .out2(demultiplexer_1_out2), .in(ram_1_data),
    .sel({and_3_out[1], decoder_2_out2[1]}));  // open: out3
  and and_6 (and_6_out, decoder_2_out6, decoder_1_out0);
  or or_3 (or_3_out, and_5_out, and_6_out);
  Register #(.width(3)) OPCODE (.D(IR_q[14:12]), .Q(OPCODE_q), .clk(decoder_2_out2[0]));  // open: en, clr
  Register #(.width(1)) I (.D(IR_q[15]), .Q(I_q), .clk(decoder_2_out2[0]));  // open: en, clr
  Decoder #(.select(3), .enable("false")) decoder_1 (
    .out0(decoder_1_out0), .out7(decoder_1_out7), .sel(OPCODE_q));  // open: out1, out2, out3, out4, out5, out6
  not not_1 (not_1_out, I_q);
  Decoder #(.select(3), .enable("false")) decoder_2 (
    .out0(decoder_2_out0), .out1(decoder_2_out1), .out2(decoder_2_out2[0]), .out3(decoder_2_out3),
    .out4(decoder_2_out4), .out5(decoder_2_out5), .out6(decoder_2_out6), .sel(SC_q));  // open: out7
  Counter #(.width(3), .max('h7)) SC (.Q(SC_q), .clk(clock_1_out), .clr(or_3_out));  // open: load, D, count, carry
  Clock clock_1 (.out(clock_1_out));
  and and_7 (and_7_out, decoder_1_out7, not_1_out, IR_q[0], IR_q[1]);
  not not_2 (not_2_out, decoder_1_out7);
  and and_8 (and_8_out, not_2_out, I_q);
  and and_9 (and_9_out, and_7_out, decoder_2_out3);

  // Notes on the sheet:
  //   T2
  //   T3
  //   D7'I
  //   PC
  //   IR(0 - 11)
  //   M[AR]
  //   D7'IT3
  //   T1
  //   M[AR]
  //   T1
  //   M[AR]
  //   T4
  //   D0
  //   DR
  //   T5
  //   D0
  //   T2
  //   D7'IT3
  //   D0T4
  //   D7I'T3B0B1
  //   CLK
  //   AC
  //   D0T5
  //   D0T5
  //   MEMORY
  //   D0T5
  //   D7I'T3B0B1
  //   D1'IT3
  //   D0T4
  //   D0
  //   I'
  //   B0
  //   B1
  //   D7
  //   D7
  //   D7I'B0B1
  //   D7'
  //   I
  //   D7I'T3B0B1
  //   T3
  //   D7'I
endmodule
